# Fritzing sketch 04-CameraTrap (saved by Fritzing 0.9.9b)
breadboards: 1

parts:
  USBUART1 = PL2303 USB UART Breakout
  Mod1 = ESP32 - CAM
  Компонент1 = Arduino Pro Mini v13  # not connected

nets:
  N1: USBUART1.TXD, Mod1.VOR

custom parts:
  PL2303 USB UART Breakout: PL2302 Usb Uart Breakout Board with Battery
  ESP32 - CAM: The ESP32-CAM has a very competitive small-size camera module that can operate independently as a minimum system with a footprint of only 27*40.5*4.5mm and a deep sleep current of up to 6mA.
